# Fritzing sketch TankSchematic (saved by Fritzing 0.9.3b)

parts:
  Part1 = Arduino Mega 2560 (Rev3)
  MD03A1 = Dual VNH2SP30 Motor Driver [part_number=MD03A]
  Part4 = Logic Level Converter
  M1 = DC Motor
  M2 = DC Motor
  U1 = LIPO-110mAh [package=lipo-110]
  U3 = LIPO-110mAh [package=lipo-110]
  U4 = LIPO-110mAh [package=lipo-110]
  U5 = Voltage Regulator - 5V [package="TO220 [THT]"]
  Raspberry_Pi_Zero1 = Raspberry Pi Zero
  U6 = NodeMCU V1.0
  Part3 = Bluetooth HC-05 Macho
  Part5 = 10-DOF IMU L3GD20H + LSM303 + BMP180 [part_number=1604]
  S1 = Toggle Switch [package=THT]
  J1 = Basic Servo  # not connected
  J2 = Basic Servo  # not connected

nets:
  N1: Part1.A0, MD03A1.1CS
  N2: Part1.A1, MD03A1.2CS
  N3: Part1.D21/SCL, Part4.TX2_HV, Part5.SCL
  N4: Part1.D20/SDA, Part4.RX2_HV, Part5.SDA
  GND: Part1.GND, MD03A1.GND#136, Part4.GND, U6.GND, Part3.GND, Part5.GND
  VIN: Part1.5V, MD03A1.+5V_(IN), Part4.HV, U6.Vin, Part3.VCC, Part5.VIN
  N5: Part1.VIN, S1.L1
  N6: Part1.D0_RX0, Part3.TXD
  N7: Part1.D1_TX0, Part3.RXD
  N8: Part1.D2_PWM, Part4.RX_HV
  N9: Part1.D3_PWM, MD03A1.PWM
  N10: Part1.D5_PWM, MD03A1.2PWM
  N11: Part1.D30, MD03A1.1DIAG/EN
  N12: Part1.D31, MD03A1.2DIAG/EN
  N13: Part1.D32, MD03A1.1INa
  N14: Part1.D33, MD03A1.2INb#142
  N15: Part1.D34, MD03A1.1INb
  N16: Part1.D35, MD03A1.2INb#143
  N17: MD03A1.VIN#134, U5.input_voltage
  GND_2: MD03A1.GND#138, U5.GND, Raspberry_Pi_Zero1.GND
  N18: MD03A1.VIN#139, S1.COM
  N19: MD03A1.OUT_1A, M2.pin_1
  N20: MD03A1.OUT_1B, M2.pin_2
  N21: MD03A1.OUT_2A, M1.pin_1
  N22: MD03A1.OUT_2B, M1.pin_2
  N23: MD03A1.VIN#150, U4.+
  N24: MD03A1.GND#151, U1.-
  N25: Part4.TX2_LV, Raspberry_Pi_Zero1.GPIO3, U6.D8
  N26: Part4.RX2_LV, Raspberry_Pi_Zero1.GPIO2, U6.D7
  N27: Part4.LV, U6.3V3
  N28: Part4.RX_LV, U6.D3
  N29: U1.+, U3.-
  N30: U3.+, U4.-
  N31: U5.output_voltage, Raspberry_Pi_Zero1.5V

custom parts:
  NodeMCU V1.0: ESP8266 based NodeMCU
  10-DOF IMU L3GD20H + LSM303 + BMP180: This inertial-measurement-unit combines 3 of the best quality sensors available on the market to give you 11 axes of data: 3 axes of accelerometer data, 3 axes gyroscopic, 3 axes magnetic (compass), barometric pressure/altitude and temperature. We tested many different 'combination' sensors and found these were the best value, with stable and reliable readings.
